// Logisim project 6.2_11.circ as structural Verilog: 1 circuit, main circuit main
module main (
  input  in_1,
  input  in_2,
  input  [3:0] in_3,
  input  [3:0] in_4,
  input  [3:0] in_5,
  input  [3:0] in_6,
  output [3:0] out_7
);

  wire not_1_out, not_2_out;
  wire [3:0] and_1_out, and_2_out, and_3_out, and_4_out, bit_extender_1_out, bit_extender_2_out,
       bit_extender_3_out, bit_extender_4_out;

  not not_1 (not_1_out, in_2);
  assign bit_extender_1_out = {{3{in_2}}, in_2};  // Bit_Extender bit_extender_1
  not not_2 (not_2_out, in_1);
  assign bit_extender_2_out = {{3{in_1}}, in_1};  // Bit_Extender bit_extender_2
  assign bit_extender_3_out = {{3{not_1_out}}, not_1_out};  // Bit_Extender bit_extender_3
  assign bit_extender_4_out = {{3{not_2_out}}, not_2_out};  // Bit_Extender bit_extender_4
  assign and_1_out = in_3 & bit_extender_3_out & bit_extender_4_out;  // AND_Gate and_1, 4 bits wide
  assign and_2_out = in_4 & bit_extender_3_out & bit_extender_2_out;  // AND_Gate and_2, 4 bits wide
  assign and_3_out = in_5 & bit_extender_1_out & bit_extender_4_out;  // AND_Gate and_3, 4 bits wide
  assign and_4_out = in_6 & bit_extender_1_out & bit_extender_2_out;  // AND_Gate and_4, 4 bits wide
  assign out_7 = and_1_out | and_2_out | and_3_out | and_4_out;  // OR_Gate or_1, 4 bits wide
endmodule
