// Logisim project 6.3_3.circ as structural Verilog: 1 circuit, main circuit main
module main (
  input  in_1,
  input  in_2,
  input  in_3,
  input  in_4,
  input  in_5,
  input  in_6,
  input  in_7,
  input  in_8,
  output out_9,
  output out_10,
  output out_11
);

  wire not_1_out, not_2_out, not_3_out, not_4_out, not_5_out, not_6_out, not_7_out;

  not not_1 (not_1_out, in_2);
  not not_2 (not_2_out, in_3);
  not not_3 (not_3_out, in_4);
  not not_4 (not_4_out, in_5);
  not not_5 (not_5_out, in_6);
  not not_6 (not_6_out, in_7);
  not not_7 (not_7_out, in_8);
  and and_1 (out_9, not_4_out, not_5_out, not_6_out, not_7_out);
  and and_2 (out_10, not_2_out, not_3_out, not_6_out, not_7_out);
  and and_3 (out_11, not_1_out, not_3_out, not_5_out, not_7_out);
endmodule
